# Fritzing sketch lightsaber (saved by Fritzing 0.9.3b)

parts:
  R2 = Resistor [tolerance=±5% resistance=10k package=THT]
  S1 = Pushbutton [package=THT]
  LED2 = Super Flux LED blue [color=Green]
  Q1 = PNP-Transistor [package="TO92 [THT]"]
  U1 = LIPO-2000mAh [package=lipo-2000]
  GY1 = MPU-6050 Board GY-521 [form="♀ (female)" package=THT]
  DFPlayer_Mini1 = DFPlayer MINI [package="DIP (Dual Inline) [THT]"]
  Componente1 = Arduino Pro Mini (5V)
  SP1 = SPEAKER [package=pcb_mount_speaker]
  LED3 = LED - 5mm [color="Red (633nm)" package="5 mm [THT]"]
  R3 = Resistor [tolerance=±5% resistance=220 package=THT]

nets:
  GND: R2.Pin_0, Q1.C, U1.-, GY1.pin2, DFPlayer_Mini1.GND, DFPlayer_Mini1.SPK2, Componente1.GND, SP1.-, R3.Pin_1
  N1: R2.Pin_1, S1.leg0, Componente1.D9
  N2: S1.leg1, GY1.pin1, Componente1.VCC
  N3: LED2.anode, U1.+, DFPlayer_Mini1.VCC, DFPlayer_Mini1.RX, Componente1.RAW, Componente1.TXO
  N4: LED2.cathode, Q1.B
  N5: Q1.E, Componente1.D10
  N6: GY1.pin3, Componente1.A4
  N7: GY1.pin4, Componente1.A5
  N8: DFPlayer_Mini1.TX, Componente1.RXI
  N9: DFPlayer_Mini1.SPK1, SP1.+
  N10: Componente1.MOSI, LED3.anode
  N11: LED3.cathode, R3.Pin_0

custom parts:
  MPU-6050 Board GY-521: Acelerometro y Giroscopio MPU-6050 Board GY-521
  DFPlayer MINI: MP3 module by DFRobot.com for playing Music from an SD-Card. Supports WAV and MP3 files.

// code stored in the sketch: Untitled2.ino
void setup() {   
 pinMode(11, OUTPUT); 
}

 loop() { 
  digitalWrite(11, HIGH);  
 delay(1000);    
digitalWrite(11, LOW); 
delay(1000); 
}
